// Logisim project full adder using three input nand gate.circ as structural Verilog: 1 circuit, main circuit main
module main (
  input  in_1,
  input  in_2,
  input  in_3,
  output out_4,
  output out_5
);

  wire and_1_out, and_2_out, and_3_out;

  ExactlyOne xor_1 (.out(out_4), .in0(in_1), .in2(in_2), .in4(in_3));
  and and_1 (and_1_out, in_1, in_2);
  and and_2 (and_2_out, in_1, in_3);
  and and_3 (and_3_out, in_2, in_3);
  or or_1 (out_5, and_1_out, and_2_out, and_3_out);
endmodule
